// Logisim project charCreator.circ as structural Verilog: 1 circuit, main circuit main
module main (
  input  [7:0] in_1,
  input  [7:0] in_2,
  input  [7:0] in_3,
  input  [7:0] in_4,
  input  [7:0] in_5
);

  DotMatrix #(.matrixrows(8)) dotmatrix_1 (.col0(in_1), .col1(in_2), .col2(in_3), .col3(in_4), .col4(in_5));
  // Probe on in_1
  // Probe on in_2
  // Probe on in_3
  // Probe on in_4
  // Probe on in_5
endmodule
